// Logisim project CircuitProject.circ as structural Verilog: 3 circuits, main circuit main
module main (
  input  SW14,
  input  SW13,
  input  SW12,
  input  SW11,
  input  SW10,
  input  SW9,
  input  SW8,
  input  SW15,
  input  SW6,
  input  SW5,
  input  SW4,
  input  SW3,
  input  SW2,
  input  SW1,
  input  SW0,
  input  SW7,
  output [15:0] out_17,
  output z1,
  output z0
);

  wire and_1_out, and_2_out, and_3_out, and_4_out, and_5_out, and_6_out, and_7_out, and_8_out, and_9_out,
       and_10_out, BTNL_out, BTNR_out, clk_out, comparator_1_gt, comparator_2_gt, comparator_3_gt,
       comparator_4_gt, comparator_5_gt, comparator_6_gt, comparator_7_gt, comparator_8_gt, comparator_9_gt,
       comparator_10_gt, comparator_11_gt, comparator_12_gt, comparator_13_gt, comparator_14_gt,
       comparator_15_gt, comparator_16_gt, comparator_17_gt, comparator_18_gt, comparator_19_gt,
       comparator_20_gt, comparator_21_gt, comparator_22_gt, comparator_23_gt, comparator_24_gt,
       comparator_25_gt, comparator_26_gt, custom_7_segment_decoder_1_a, custom_7_segment_decoder_1_b,
       custom_7_segment_decoder_1_c, custom_7_segment_decoder_1_d, custom_7_segment_decoder_1_e,
       custom_7_segment_decoder_1_f, custom_7_segment_decoder_1_g, custom_7_segment_decoder_2_a,
       custom_7_segment_decoder_2_b, custom_7_segment_decoder_2_c, custom_7_segment_decoder_2_d,
       custom_7_segment_decoder_2_e, custom_7_segment_decoder_2_f, custom_7_segment_decoder_2_g,
       custom_7_segment_decoder_3_a, custom_7_segment_decoder_3_b, custom_7_segment_decoder_3_c,
       custom_7_segment_decoder_3_d, custom_7_segment_decoder_3_e, custom_7_segment_decoder_3_f,
       custom_7_segment_decoder_3_g, nor_1_out, not_1_out, not_2_out, not_3_out, not_4_out, not_5_out,
       not_6_out, or_1_out, or_2_out, or_3_out, or_4_out, or_5_out, or_6_out, or_7_out, or_8_out, or_9_out,
       or_10_out, or_11_out, or_12_out, or_13_out, register_1_q, shift_register_1_p1, shift_register_2_p23,
       shift_register_2_p24, shift_register_2_p25, shift_register_2_p26, shift_register_2_p27,
       shift_register_2_p28, shift_register_2_p29, shift_register_2_p30, xor_1_out, y0_qn, y1_qn;
  wire [0:0] undriven_2, undriven_3, undriven_4, undriven_5, undriven_6, undriven_7, undriven_8, undriven_9,
       undriven_10, undriven_11, undriven_12;
  wire [1:0] multiplexer_30_out;
  wire [2:0] undriven;
  wire [3:0] adder_2_out, adder_3_out, adder_4_out, adder_5_out, adder_6_out, adder_7_out, adder_8_out,
       adder_9_out, adder_10_out, adder_11_out, adder_12_out, adder_13_out, adder_14_out, adder_15_out,
       adder_16_out, adder_17_out, adder_18_out, adder_19_out, adder_20_out, adder_21_out, adder_22_out,
       adder_23_out, adder_24_out, adder_25_out, adder_26_out, adder_27_out, multiplexer_4_out,
       multiplexer_5_out, multiplexer_6_out, multiplexer_7_out, multiplexer_8_out, multiplexer_9_out,
       multiplexer_10_out, multiplexer_11_out, multiplexer_12_out, multiplexer_13_out, multiplexer_14_out,
       multiplexer_15_out, multiplexer_16_out, multiplexer_17_out, multiplexer_18_out, multiplexer_19_out,
       multiplexer_20_out, multiplexer_21_out, multiplexer_22_out, multiplexer_23_out, multiplexer_24_out,
       multiplexer_25_out, multiplexer_26_out, multiplexer_27_out, multiplexer_28_out, multiplexer_29_out,
       multiplexer_31_out, multiplexer_32_out, multiplexer_33_out;
  wire [6:0] multiplexer_34_out;
  wire [7:0] multiplexer_1_out, multiplexer_2_out;
  wire [7:1] xor_2_out, xor_9_out;
  wire [15:0] adder_1_out, multiplexer_3_out, shift_register_1_p14;

  Clock clk (.out(clk_out));
  or or_1 (or_1_out, SW11, or_5_out);
  or or_2 (or_2_out, SW12, or_1_out);
  or or_3 (or_3_out, SW13, or_2_out);
  or or_4 (or_4_out, SW9, SW8);
  or or_5 (or_5_out, SW10, or_4_out);
  or or_6 (or_6_out, SW4, or_10_out);
  or or_7 (or_7_out, SW5, or_6_out);
  Register #(.width(1)) register_1 (
    .D(xor_1_out), .en(shift_register_1_p1), .clk(clk_out), .Q(register_1_q));  // open: clr
  xor xor_1 (xor_1_out, SW7, SW15);
  xor xor_2 (xor_2_out[1], SW8, SW9);
  xor xor_3 (xor_2_out[2], or_4_out, SW10);
  xor xor_4 (xor_2_out[3], or_5_out, SW11);
  xor xor_5 (xor_2_out[4], or_1_out, SW12);
  xor xor_6 (xor_2_out[5], or_2_out, SW13);
  xor xor_7 (xor_2_out[6], or_3_out, SW14);
  xor xor_8 (xor_2_out[7], or_3_out, SW15);
  or or_8 (or_8_out, SW1, SW0);
  or or_9 (or_9_out, SW2, or_8_out);
  or or_10 (or_10_out, SW3, or_9_out);
  xor xor_9 (xor_9_out[1], SW0, SW1);
  xor xor_10 (xor_9_out[2], or_8_out, SW2);
  xor xor_11 (xor_9_out[3], or_9_out, SW3);
  xor xor_12 (xor_9_out[4], or_10_out, SW4);
  xor xor_13 (xor_9_out[5], or_6_out, SW5);
  xor xor_14 (xor_9_out[6], or_7_out, SW6);
  xor xor_15 (xor_9_out[7], or_7_out, SW7);
  Multiplexer #(.width(8)) multiplexer_1 (
    .in0({SW15, SW14, SW13, SW12, SW11, SW10, SW9, SW8}), .in1({xor_2_out, SW8}), .out(multiplexer_1_out),
    .sel(SW15));
  not not_1 (not_1_out, shift_register_1_p1);
  not not_2 (not_2_out, shift_register_1_p1);
  Multiplexer #(.width(8)) multiplexer_2 (
    .in0({SW7, SW6, SW5, SW4, SW3, SW2, SW1, SW0}), .in1({xor_9_out, SW0}), .out(multiplexer_2_out), .sel(SW7));
  // Shift_Register #(.length(16)) shift_register_1: pin names not known; wires that end beside it: shift_register_1_p1, not_1_out, clk_out, 1'b0, multiplexer_1_out[0], multiplexer_1_out[1], multiplexer_1_out[2], multiplexer_1_out[3], multiplexer_1_out[4], multiplexer_1_out[5], multiplexer_1_out[6], multiplexer_1_out[7], 1'b0, shift_register_1_p14[0], shift_register_1_p14[1], shift_register_1_p14[2], shift_register_1_p14[3], shift_register_1_p14[4], shift_register_1_p14[5], shift_register_1_p14[6]
  // Shift_Register shift_register_2: pin names not known; wires that end beside it: 1'b0, shift_register_1_p1, not_2_out, clk_out, 1'b0, multiplexer_2_out[7], multiplexer_2_out[6], multiplexer_2_out[5], multiplexer_2_out[4], multiplexer_2_out[3], multiplexer_2_out[2], multiplexer_2_out[1], multiplexer_2_out[0], shift_register_1_p14[7], shift_register_1_p14[8], shift_register_1_p14[9], shift_register_1_p14[10], shift_register_1_p14[11], shift_register_1_p14[12], shift_register_1_p14[13], shift_register_1_p14[14], shift_register_1_p14[15], shift_register_2_p23, shift_register_2_p24, shift_register_2_p25, shift_register_2_p26, shift_register_2_p27, shift_register_2_p28, shift_register_2_p29, shift_register_2_p30
  nor nor_1 (nor_1_out, shift_register_2_p23, shift_register_2_p24, shift_register_2_p25, shift_register_2_p26, shift_register_2_p27, shift_register_2_p28, shift_register_2_p29, shift_register_2_p30);
  not not_3 (not_3_out, shift_register_1_p1);
  Adder #(.width(16)) adder_1 (.a(out_17), .b(shift_register_1_p14), .out(adder_1_out), .cin(1'b0));  // open: cout
  Button BTNC (.out(shift_register_1_p1));
  Register #(.width(16)) register_2 (.D(multiplexer_3_out), .en(or_11_out), .clk(clk_out), .Q(out_17));  // open: clr
  Multiplexer #(.width(16)) multiplexer_3 (
    .in0({16{1'b0}}), .in1(adder_1_out), .out(multiplexer_3_out), .sel(not_3_out));
  or or_11 (or_11_out, not_4_out, shift_register_2_p30);
  not not_4 (not_4_out, not_3_out);
  Adder #(.width(4)) adder_2 (.a(4'b0011), .b({1'b0, undriven}), .out(adder_2_out));  // open: cin, cout
  Multiplexer #(.width(4)) multiplexer_4 (
    .in0({1'b0, undriven}), .in1(adder_2_out), .out(multiplexer_4_out), .sel(comparator_1_gt));
  Comparator #(.mode("unsigned"), .width(4)) comparator_1 (
    .a({1'b0, undriven}), .b(4'b0100), .gt(comparator_1_gt));  // open: eq, lt
  Adder #(.width(4)) adder_3 (
    .a(4'b0011), .b({multiplexer_4_out[2:0], undriven_2[0]}), .out(adder_3_out));  // open: cin, cout
  Comparator #(.mode("unsigned"), .width(4)) comparator_2 (
    .a({multiplexer_4_out[2:0], undriven_2[0]}), .b(4'b0100), .gt(comparator_2_gt));  // open: eq, lt
  Multiplexer #(.width(4)) multiplexer_5 (
    .in0({multiplexer_4_out[2:0], undriven_2[0]}), .in1(adder_3_out), .out(multiplexer_5_out),
    .sel(comparator_2_gt));
  Adder #(.width(4)) adder_4 (
    .a(4'b0011), .b({multiplexer_5_out[2:0], undriven_3[0]}), .out(adder_4_out));  // open: cin, cout
  Comparator #(.mode("unsigned"), .width(4)) comparator_3 (
    .a({multiplexer_5_out[2:0], undriven_3[0]}), .b(4'b0100), .gt(comparator_3_gt));  // open: eq, lt
  Multiplexer #(.width(4)) multiplexer_6 (
    .in0({multiplexer_5_out[2:0], undriven_3[0]}), .in1(adder_4_out), .out(multiplexer_6_out),
    .sel(comparator_3_gt));
  Adder #(.width(4)) adder_5 (
    .a(4'b0011), .b({multiplexer_6_out[2:0], undriven_4[0]}), .out(adder_5_out));  // open: cin, cout
  Comparator #(.mode("unsigned"), .width(4)) comparator_4 (
    .a({multiplexer_6_out[2:0], undriven_4[0]}), .b(4'b0100), .gt(comparator_4_gt));  // open: eq, lt
  Adder #(.width(4)) adder_6 (
    .a(4'b0011), .b({1'b0, multiplexer_4_out[3], multiplexer_5_out[3], multiplexer_6_out[3]}),
    .out(adder_6_out));  // open: cin, cout
  Multiplexer #(.width(4)) multiplexer_7 (
    .in0({multiplexer_6_out[2:0], undriven_4[0]}), .in1(adder_5_out), .out(multiplexer_7_out),
    .sel(comparator_4_gt));
  Multiplexer #(.width(4)) multiplexer_8 (
    .in0({1'b0, multiplexer_4_out[3], multiplexer_5_out[3], multiplexer_6_out[3]}), .in1(adder_6_out),
    .out(multiplexer_8_out), .sel(comparator_5_gt));
  Comparator #(.mode("unsigned"), .width(4)) comparator_5 (
    .a({1'b0, multiplexer_4_out[3], multiplexer_5_out[3], multiplexer_6_out[3]}), .b(4'b0100),
    .gt(comparator_5_gt));  // open: eq, lt
  Adder #(.width(4)) adder_7 (
    .a(4'b0011), .b({multiplexer_7_out[2:0], undriven_5[0]}), .out(adder_7_out));  // open: cin, cout
  Comparator #(.mode("unsigned"), .width(4)) comparator_6 (
    .a({multiplexer_7_out[2:0], undriven_5[0]}), .b(4'b0100), .gt(comparator_6_gt));  // open: eq, lt
  Adder #(.width(4)) adder_8 (
    .a(4'b0011), .b({multiplexer_8_out[2:0], multiplexer_7_out[3]}), .out(adder_8_out));  // open: cin, cout
  Multiplexer #(.width(4)) multiplexer_9 (
    .in0({multiplexer_7_out[2:0], undriven_5[0]}), .in1(adder_7_out), .out(multiplexer_9_out),
    .sel(comparator_6_gt));
  Multiplexer #(.width(4)) multiplexer_10 (
    .in0({multiplexer_8_out[2:0], multiplexer_7_out[3]}), .in1(adder_8_out), .out(multiplexer_10_out),
    .sel(comparator_7_gt));
  Comparator #(.mode("unsigned"), .width(4)) comparator_7 (
    .a({multiplexer_8_out[2:0], multiplexer_7_out[3]}), .b(4'b0100), .gt(comparator_7_gt));  // open: eq, lt
  Adder #(.width(4)) adder_9 (
    .a(4'b0011), .b({multiplexer_9_out[2:0], undriven_6[0]}), .out(adder_9_out));  // open: cin, cout
  Comparator #(.mode("unsigned"), .width(4)) comparator_8 (
    .a({multiplexer_9_out[2:0], undriven_6[0]}), .b(4'b0100), .gt(comparator_8_gt));  // open: eq, lt
  Adder #(.width(4)) adder_10 (
    .a(4'b0011), .b({multiplexer_10_out[2:0], multiplexer_9_out[3]}), .out(adder_10_out));  // open: cin, cout
  Multiplexer #(.width(4)) multiplexer_11 (
    .in0({multiplexer_9_out[2:0], undriven_6[0]}), .in1(adder_9_out), .out(multiplexer_11_out),
    .sel(comparator_8_gt));
  Multiplexer #(.width(4)) multiplexer_12 (
    .in0({multiplexer_10_out[2:0], multiplexer_9_out[3]}), .in1(adder_10_out), .out(multiplexer_12_out),
    .sel(comparator_9_gt));
  Comparator #(.mode("unsigned"), .width(4)) comparator_9 (
    .a({multiplexer_10_out[2:0], multiplexer_9_out[3]}), .b(4'b0100), .gt(comparator_9_gt));  // open: eq, lt
  Adder #(.width(4)) adder_11 (
    .a(4'b0011), .b({multiplexer_11_out[2:0], undriven_7[0]}), .out(adder_11_out));  // open: cin, cout
  Comparator #(.mode("unsigned"), .width(4)) comparator_10 (
    .a({multiplexer_11_out[2:0], undriven_7[0]}), .b(4'b0100), .gt(comparator_10_gt));  // open: eq, lt
  Adder #(.width(4)) adder_12 (
    .a(4'b0011), .b({multiplexer_12_out[2:0], multiplexer_11_out[3]}), .out(adder_12_out));  // open: cin, cout
  Button BTNL (.out(BTNL_out));
  Button BTNR (.out(BTNR_out));
  Multiplexer #(.width(4)) multiplexer_13 (
    .in0({multiplexer_11_out[2:0], undriven_7[0]}), .in1(adder_11_out), .out(multiplexer_13_out),
    .sel(comparator_10_gt));
  Multiplexer #(.width(4)) multiplexer_14 (
    .in0({multiplexer_12_out[2:0], multiplexer_11_out[3]}), .in1(adder_12_out), .out(multiplexer_14_out),
    .sel(comparator_11_gt));
  Comparator #(.mode("unsigned"), .width(4)) comparator_11 (
    .a({multiplexer_12_out[2:0], multiplexer_11_out[3]}), .b(4'b0100), .gt(comparator_11_gt));  // open: eq, lt
  Adder #(.width(4)) adder_13 (
    .a(4'b0011), .b({1'b0, multiplexer_8_out[3], multiplexer_10_out[3], multiplexer_12_out[3]}),
    .out(adder_13_out));  // open: cin, cout
  Multiplexer #(.width(4)) multiplexer_15 (
    .in0({1'b0, multiplexer_8_out[3], multiplexer_10_out[3], multiplexer_12_out[3]}), .in1(adder_13_out),
    .out(multiplexer_15_out), .sel(comparator_12_gt));
  Comparator #(.mode("unsigned"), .width(4)) comparator_12 (
    .a({1'b0, multiplexer_8_out[3], multiplexer_10_out[3], multiplexer_12_out[3]}), .b(4'b0100),
    .gt(comparator_12_gt));  // open: eq, lt
  not not_5 (not_5_out, BTNL_out);
  not not_6 (not_6_out, BTNR_out);
  Adder #(.width(4)) adder_14 (
    .a(4'b0011), .b({multiplexer_13_out[2:0], undriven_8[0]}), .out(adder_14_out));  // open: cin, cout
  Comparator #(.mode("unsigned"), .width(4)) comparator_13 (
    .a({multiplexer_13_out[2:0], undriven_8[0]}), .b(4'b0100), .gt(comparator_13_gt));  // open: eq, lt
  Adder #(.width(4)) adder_15 (
    .a(4'b0011), .b({multiplexer_14_out[2:0], multiplexer_13_out[3]}), .out(adder_15_out));  // open: cin, cout
  Multiplexer #(.width(4)) multiplexer_16 (
    .in0({multiplexer_13_out[2:0], undriven_8[0]}), .in1(adder_14_out), .out(multiplexer_16_out),
    .sel(comparator_13_gt));
  Multiplexer #(.width(4)) multiplexer_17 (
    .in0({multiplexer_14_out[2:0], multiplexer_13_out[3]}), .in1(adder_15_out), .out(multiplexer_17_out),
    .sel(comparator_14_gt));
  Comparator #(.mode("unsigned"), .width(4)) comparator_14 (
    .a({multiplexer_14_out[2:0], multiplexer_13_out[3]}), .b(4'b0100), .gt(comparator_14_gt));  // open: eq, lt
  Adder #(.width(4)) adder_16 (
    .a(4'b0011), .b({multiplexer_15_out[2:0], multiplexer_14_out[3]}), .out(adder_16_out));  // open: cin, cout
  Multiplexer #(.width(4)) multiplexer_18 (
    .in0({multiplexer_15_out[2:0], multiplexer_14_out[3]}), .in1(adder_16_out), .out(multiplexer_18_out),
    .sel(comparator_15_gt));
  Comparator #(.mode("unsigned"), .width(4)) comparator_15 (
    .a({multiplexer_15_out[2:0], multiplexer_14_out[3]}), .b(4'b0100), .gt(comparator_15_gt));  // open: eq, lt
  Adder #(.width(4)) adder_17 (
    .a(4'b0011), .b({multiplexer_16_out[2:0], undriven_9[0]}), .out(adder_17_out));  // open: cin, cout
  Comparator #(.mode("unsigned"), .width(4)) comparator_16 (
    .a({multiplexer_16_out[2:0], undriven_9[0]}), .b(4'b0100), .gt(comparator_16_gt));  // open: eq, lt
  Adder #(.width(4)) adder_18 (
    .a(4'b0011), .b({multiplexer_17_out[2:0], multiplexer_16_out[3]}), .out(adder_18_out));  // open: cin, cout
  and and_1 (and_1_out, z1, z0);
  and and_2 (and_2_out, y0_qn, BTNL_out);
  and and_3 (and_3_out, BTNL_out, not_6_out);
  and and_4 (and_4_out, not_6_out, y0_qn);
  and and_5 (and_5_out, y1_qn, BTNR_out);
  and and_6 (and_6_out, y0_qn, BTNR_out, not_5_out);
  and and_7 (and_7_out, y0_qn, and_3_out);
  and and_8 (and_8_out, not_6_out, not_5_out, z0);
  and and_9 (and_9_out, and_1_out, BTNL_out);
  Multiplexer #(.width(4)) multiplexer_19 (
    .in0({multiplexer_16_out[2:0], undriven_9[0]}), .in1(adder_17_out), .out(multiplexer_19_out),
    .sel(comparator_16_gt));
  Multiplexer #(.width(4)) multiplexer_20 (
    .in0({multiplexer_17_out[2:0], multiplexer_16_out[3]}), .in1(adder_18_out), .out(multiplexer_20_out),
    .sel(comparator_17_gt));
  Comparator #(.mode("unsigned"), .width(4)) comparator_17 (
    .a({multiplexer_17_out[2:0], multiplexer_16_out[3]}), .b(4'b0100), .gt(comparator_17_gt));  // open: eq, lt
  Adder #(.width(4)) adder_19 (
    .a(4'b0011), .b({multiplexer_18_out[2:0], multiplexer_17_out[3]}), .out(adder_19_out));  // open: cin, cout
  Multiplexer #(.width(4)) multiplexer_21 (
    .in0({multiplexer_18_out[2:0], multiplexer_17_out[3]}), .in1(adder_19_out), .out(multiplexer_21_out),
    .sel(comparator_18_gt));
  Comparator #(.mode("unsigned"), .width(4)) comparator_18 (
    .a({multiplexer_18_out[2:0], multiplexer_17_out[3]}), .b(4'b0100), .gt(comparator_18_gt));  // open: eq, lt
  or or_12 (or_12_out, and_1_out, and_2_out, and_3_out, and_4_out);
  or or_13 (or_13_out, and_5_out, and_6_out, and_7_out, and_8_out, and_9_out);
  Adder #(.width(4)) adder_20 (
    .a(4'b0011), .b({multiplexer_19_out[2:0], undriven_10[0]}), .out(adder_20_out));  // open: cin, cout
  Comparator #(.mode("unsigned"), .width(4)) comparator_19 (
    .a({multiplexer_19_out[2:0], undriven_10[0]}), .b(4'b0100), .gt(comparator_19_gt));  // open: eq, lt
  Adder #(.width(4)) adder_21 (
    .a(4'b0011), .b({multiplexer_20_out[2:0], multiplexer_19_out[3]}), .out(adder_21_out));  // open: cin, cout
  Multiplexer #(.width(4)) multiplexer_22 (
    .in0({multiplexer_19_out[2:0], undriven_10[0]}), .in1(adder_20_out), .out(multiplexer_22_out),
    .sel(comparator_19_gt));
  Multiplexer #(.width(4)) multiplexer_23 (
    .in0({multiplexer_20_out[2:0], multiplexer_19_out[3]}), .in1(adder_21_out), .out(multiplexer_23_out),
    .sel(comparator_20_gt));
  Comparator #(.mode("unsigned"), .width(4)) comparator_20 (
    .a({multiplexer_20_out[2:0], multiplexer_19_out[3]}), .b(4'b0100), .gt(comparator_20_gt));  // open: eq, lt
  Adder #(.width(4)) adder_22 (
    .a(4'b0011), .b({multiplexer_21_out[2:0], multiplexer_20_out[3]}), .out(adder_22_out));  // open: cin, cout
  Multiplexer #(.width(4)) multiplexer_24 (
    .in0({multiplexer_21_out[2:0], multiplexer_20_out[3]}), .in1(adder_22_out), .out(multiplexer_24_out),
    .sel(comparator_21_gt));
  Comparator #(.mode("unsigned"), .width(4)) comparator_21 (
    .a({multiplexer_21_out[2:0], multiplexer_20_out[3]}), .b(4'b0100), .gt(comparator_21_gt));  // open: eq, lt
  Adder #(.width(4)) adder_23 (
    .a(4'b0011), .b({1'b0, multiplexer_15_out[3], multiplexer_18_out[3], multiplexer_21_out[3]}),
    .out(adder_23_out));  // open: cin, cout
  Comparator #(.mode("unsigned"), .width(4)) comparator_22 (
    .a({1'b0, multiplexer_15_out[3], multiplexer_18_out[3], multiplexer_21_out[3]}), .b(4'b0100),
    .gt(comparator_22_gt));  // open: eq, lt
  D_Flip_Flop y1 (.D(or_12_out), .clk(clk_out), .Q(z1), .Qn(y1_qn));  // open: preset, reset
  D_Flip_Flop y0 (.D(or_13_out), .clk(clk_out), .Q(z0), .Qn(y0_qn));  // open: preset, reset
  Adder #(.width(4)) adder_24 (
    .a(4'b0011), .b({multiplexer_22_out[2:0], undriven_11[0]}), .out(adder_24_out));  // open: cin, cout
  Comparator #(.mode("unsigned"), .width(4)) comparator_23 (
    .a({multiplexer_22_out[2:0], undriven_11[0]}), .b(4'b0100), .gt(comparator_23_gt));  // open: eq, lt
  Adder #(.width(4)) adder_25 (
    .a(4'b0011), .b({multiplexer_23_out[2:0], multiplexer_22_out[3]}), .out(adder_25_out));  // open: cin, cout
  Multiplexer #(.width(4)) multiplexer_25 (
    .in0({1'b0, multiplexer_15_out[3], multiplexer_18_out[3], multiplexer_21_out[3]}), .in1(adder_23_out),
    .out(multiplexer_25_out), .sel(comparator_22_gt));
  Multiplexer #(.width(4)) multiplexer_26 (
    .in0({multiplexer_22_out[2:0], undriven_11[0]}), .in1(adder_24_out), .out(multiplexer_26_out),
    .sel(comparator_23_gt));
  Multiplexer #(.width(4)) multiplexer_27 (
    .in0({multiplexer_23_out[2:0], multiplexer_22_out[3]}), .in1(adder_25_out), .out(multiplexer_27_out),
    .sel(comparator_24_gt));
  Comparator #(.mode("unsigned"), .width(4)) comparator_24 (
    .a({multiplexer_23_out[2:0], multiplexer_22_out[3]}), .b(4'b0100), .gt(comparator_24_gt));  // open: eq, lt
  Adder #(.width(4)) adder_26 (
    .a(4'b0011), .b({multiplexer_24_out[2:0], multiplexer_23_out[3]}), .out(adder_26_out));  // open: cin, cout
  Multiplexer #(.width(4)) multiplexer_28 (
    .in0({multiplexer_24_out[2:0], multiplexer_23_out[3]}), .in1(adder_26_out), .out(multiplexer_28_out),
    .sel(comparator_25_gt));
  Comparator #(.mode("unsigned"), .width(4)) comparator_25 (
    .a({multiplexer_24_out[2:0], multiplexer_23_out[3]}), .b(4'b0100), .gt(comparator_25_gt));  // open: eq, lt
  Adder #(.width(4)) adder_27 (
    .a(4'b0011), .b({multiplexer_25_out[2:0], multiplexer_24_out[3]}), .out(adder_27_out));  // open: cin, cout
  Comparator #(.mode("unsigned"), .width(4)) comparator_26 (
    .a({multiplexer_25_out[2:0], multiplexer_24_out[3]}), .b(4'b0100), .gt(comparator_26_gt));  // open: eq, lt
  Multiplexer #(.width(4)) multiplexer_29 (
    .in0({multiplexer_25_out[2:0], multiplexer_24_out[3]}), .in1(adder_27_out), .out(multiplexer_29_out),
    .sel(comparator_26_gt));
  Multiplexer #(.width(2)) multiplexer_30 (.in0(2'b00), .in1({z1, z0}), .out(multiplexer_30_out), .sel(and_10_out));
  and and_10 (and_10_out, nor_1_out, not_3_out);
  Multiplexer #(.select(2), .width(4)) multiplexer_31 (
    .in0(4'b1111), .in1({multiplexer_26_out[2:0], undriven_12[0]}),
    .in2({multiplexer_27_out[2:0], multiplexer_26_out[3]}),
    .in3({multiplexer_28_out[2:0], multiplexer_27_out[3]}), .out(multiplexer_31_out), .sel(multiplexer_30_out));
  Multiplexer #(.select(2), .width(4)) multiplexer_32 (
    .in0(4'b1111), .in1({multiplexer_27_out[2:0], multiplexer_26_out[3]}),
    .in2({multiplexer_28_out[2:0], multiplexer_27_out[3]}),
    .in3({multiplexer_29_out[2:0], multiplexer_28_out[3]}), .out(multiplexer_32_out), .sel(multiplexer_30_out));
  Multiplexer #(.select(2), .width(4)) multiplexer_33 (
    .in0(4'b1111), .in1({multiplexer_28_out[2:0], multiplexer_27_out[3]}),
    .in2({multiplexer_29_out[2:0], multiplexer_28_out[3]}),
    .in3({2'b00, multiplexer_25_out[3], multiplexer_29_out[3]}), .out(multiplexer_33_out),
    .sel(multiplexer_30_out));
  Custom_7_Segment_Decoder custom_7_segment_decoder_1 (
    .dataIn(multiplexer_33_out), .a(custom_7_segment_decoder_1_a), .b(custom_7_segment_decoder_1_b),
    .c(custom_7_segment_decoder_1_c), .d(custom_7_segment_decoder_1_d), .e(custom_7_segment_decoder_1_e),
    .f(custom_7_segment_decoder_1_f), .g(custom_7_segment_decoder_1_g));
  Custom_7_Segment_Decoder custom_7_segment_decoder_2 (
    .dataIn(multiplexer_32_out), .a(custom_7_segment_decoder_2_a), .b(custom_7_segment_decoder_2_b),
    .c(custom_7_segment_decoder_2_c), .d(custom_7_segment_decoder_2_d), .e(custom_7_segment_decoder_2_e),
    .f(custom_7_segment_decoder_2_f), .g(custom_7_segment_decoder_2_g));
  Multiplexer #(.width(7)) multiplexer_34 (
    .in0({7{1'b1}}), .in1(7'b0111111), .out(multiplexer_34_out), .sel(register_1_q));
  Custom_7_Segment_Decoder custom_7_segment_decoder_3 (
    .dataIn(multiplexer_31_out), .a(custom_7_segment_decoder_3_a), .b(custom_7_segment_decoder_3_b),
    .c(custom_7_segment_decoder_3_c), .d(custom_7_segment_decoder_3_d), .e(custom_7_segment_decoder_3_e),
    .f(custom_7_segment_decoder_3_f), .g(custom_7_segment_decoder_3_g));
  _7_Segment_Display #(.active("false")) u_7_segment_display_1 (
    .g(multiplexer_34_out[6]), .f(multiplexer_34_out[5]), .a(multiplexer_34_out[0]),
    .b(multiplexer_34_out[1]), .e(multiplexer_34_out[4]), .d(multiplexer_34_out[3]),
    .c(multiplexer_34_out[2]), .dp(1'b1));
  _7_Segment_Display #(.active("false"), .decimalPoint("false")) u_7_segment_display_2 (
    .g(custom_7_segment_decoder_1_g), .f(custom_7_segment_decoder_1_f), .a(custom_7_segment_decoder_1_a),
    .b(custom_7_segment_decoder_1_b), .e(custom_7_segment_decoder_1_e), .d(custom_7_segment_decoder_1_d),
    .c(custom_7_segment_decoder_1_c));
  _7_Segment_Display #(.active("false"), .decimalPoint("false")) u_7_segment_display_3 (
    .g(custom_7_segment_decoder_2_g), .f(custom_7_segment_decoder_2_f), .a(custom_7_segment_decoder_2_a),
    .b(custom_7_segment_decoder_2_b), .e(custom_7_segment_decoder_2_e), .d(custom_7_segment_decoder_2_d),
    .c(custom_7_segment_decoder_2_c));
  _7_Segment_Display #(.active("false"), .decimalPoint("false")) u_7_segment_display_4 (
    .g(custom_7_segment_decoder_3_g), .f(custom_7_segment_decoder_3_f), .a(custom_7_segment_decoder_3_a),
    .b(custom_7_segment_decoder_3_b), .e(custom_7_segment_decoder_3_e), .d(custom_7_segment_decoder_3_d),
    .c(custom_7_segment_decoder_3_c));

  // Notes on the sheet:
  //   LI
  //   LI (bar)
  //   LI
  //   LI
  //   LI (bar)
  //   LI (bar)
  //   Z
  //   b0
  //   Lp
  //   Z_flag
  //   BTNC (bar)
  //   DS
endmodule

module Custom_7_Segment_Decoder (
  input  [3:0] dataIn,
  output a,
  output b,
  output c,
  output d,
  output e,
  output f,
  output g
);

  wire and_1_out, and_2_out, and_3_out, and_4_out, and_5_out, and_6_out, and_7_out, and_8_out, and_9_out,
       and_10_out, and_11_out, and_12_out, and_13_out, and_14_out, and_15_out, and_16_out, and_17_out,
       not_1_out, not_2_out, not_3_out, not_4_out;

  not not_1 (not_1_out, dataIn[3]);
  not not_2 (not_2_out, dataIn[2]);
  not not_3 (not_3_out, dataIn[1]);
  not not_4 (not_4_out, dataIn[0]);
  and and_1 (and_1_out, not_1_out, not_2_out, not_3_out, dataIn[0]);
  and and_2 (and_2_out, dataIn[2], not_3_out, not_4_out);
  and and_3 (and_3_out, dataIn[3], dataIn[1]);
  and and_4 (and_4_out, dataIn[2], not_3_out, dataIn[0]);
  and and_5 (and_5_out, dataIn[2], dataIn[1], not_4_out);
  and and_6 (and_6_out, dataIn[3], dataIn[1]);
  and and_7 (and_7_out, not_2_out, dataIn[1], not_4_out);
  and and_8 (and_8_out, dataIn[3], dataIn[1]);
  and and_9 (and_9_out, not_1_out, not_2_out, not_3_out, dataIn[0]);
  and and_10 (and_10_out, dataIn[2], not_3_out, not_4_out);
  and and_11 (and_11_out, not_1_out, dataIn[2], dataIn[1], dataIn[0]);
  and and_12 (and_12_out, dataIn[2], not_3_out);
  and and_13 (and_13_out, not_1_out, not_2_out, dataIn[0]);
  and and_14 (and_14_out, not_2_out, dataIn[1]);
  and and_15 (and_15_out, dataIn[1], dataIn[0]);
  and and_16 (and_16_out, not_1_out, not_2_out, not_3_out);
  and and_17 (and_17_out, dataIn[2], dataIn[1], dataIn[0]);
  or or_1 (a, and_1_out, and_2_out, and_3_out);
  or or_2 (b, and_4_out, and_5_out, and_6_out);
  or or_3 (c, and_7_out, and_8_out);
  or or_4 (d, and_9_out, and_10_out, and_11_out);
  or or_5 (e, dataIn[0], and_12_out);
  or or_6 (f, and_13_out, and_14_out, and_15_out);
  or or_7 (g, and_16_out, and_17_out);
endmodule

module greaterThan4Add3 (
  input  in_0,
  input  in_1,
  input  in_2,
  input  in_3,
  output output_0,
  output output_1,
  output output_2,
  output output_3
);

  wire comparator_1_gt;
  wire [3:0] adder_1_out;

  Adder #(.width(4)) adder_1 (.a(4'b0011), .b({in_3, in_2, in_1, in_0}), .out(adder_1_out));  // open: cin, cout
  Multiplexer #(.width(4)) multiplexer_1 (
    .in0({in_3, in_2, in_1, in_0}), .in1(adder_1_out), .out({output_3, output_2, output_1, output_0}),
    .sel(comparator_1_gt));
  Comparator #(.mode("unsigned"), .width(4)) comparator_1 (
    .a({in_3, in_2, in_1, in_0}), .b(4'b0100), .gt(comparator_1_gt));  // open: eq, lt
endmodule
